// Logisim project Part1.circ as structural Verilog: 7 circuits, main circuit main
module main (
  input  in_1,
  input  in_2,
  input  in_3,
  input  in_4,
  input  in_5,
  input  in_6,
  input  in_7,
  input  in_8,
  input  in_9,
  input  in_10,
  input  in_11,
  input  in_12,
  input  in_13,
  input  in_14,
  input  in_15,
  output out_16,
  output out_17,
  output out_18,
  output [7:0] out_19,
  output [7:0] out_20,
  output out_21,
  output out_22
);

  AddMachine Yeet (.out_1(out_20), .out_2(out_19));
  XOR1 xor1_1 (.in_1(in_1), .in_2(in_3), .out_3(out_16));
  NAND1 nand1_1 (.in_1(in_8), .in_2(in_10), .out_3(out_18));
  NOR1 nor1_1 (.in_1(in_11), .in_2(in_12), .out_3(out_21));
  MUX2to1 mux2to1_1 (.S(in_13), .A(in_14), .B(in_15), .out_4(out_22));
  MUX4to1 mux4to1_1 (.S1(in_2), .S0(in_4), .A(in_5), .B(in_6), .C(in_7), .D(in_9), .out_7(out_17));
endmodule

module NAND1 (
  input  in_1,
  input  in_2,
  output out_3
);

  wire and_1_out;

  and and_1 (and_1_out, in_1, in_2);
  not not_1 (out_3, and_1_out);
endmodule

module NOR1 (
  input  in_1,
  input  in_2,
  output out_3
);

  wire or_1_out;

  or or_1 (or_1_out, in_1, in_2);
  not not_1 (out_3, or_1_out);
endmodule

module XOR1 (
  input  in_1,
  input  in_2,
  output out_3
);

  wire and_1_out, and_2_out, not_1_out, not_2_out;

  not not_1 (not_1_out, in_2);
  and and_1 (and_1_out, not_1_out, in_1);
  and and_2 (and_2_out, in_2, not_2_out);
  not not_2 (not_2_out, in_1);
  or or_1 (out_3, and_1_out, and_2_out);
endmodule

module MUX2to1 (
  input  S,
  input  A,
  input  B,
  output out_4
);

  wire and_1_out, and_2_out, not_1_out;

  not not_1 (not_1_out, S);
  and and_1 (and_1_out, A, not_1_out);
  and and_2 (and_2_out, S, B);
  or or_1 (out_4, and_1_out, and_2_out);
endmodule

module MUX4to1 (
  input  S1,
  input  S0,
  input  A,
  input  B,
  input  C,
  input  D,
  output out_7
);

  wire and_1_out, and_2_out, and_3_out, and_4_out, and_5_out, and_6_out, not_1_out, not_2_out, not_3_out,
       or_1_out, or_2_out;

  not not_1 (not_1_out, S1);
  not not_2 (not_2_out, S1);
  and and_1 (and_1_out, not_1_out, A);
  and and_2 (and_2_out, S1, B);
  and and_3 (and_3_out, not_2_out, C);
  and and_4 (and_4_out, S1, D);
  or or_1 (or_1_out, and_1_out, and_2_out);
  not not_3 (not_3_out, S0);
  or or_2 (or_2_out, and_3_out, and_4_out);
  and and_5 (and_5_out, or_1_out, not_3_out);
  and and_6 (and_6_out, S0, or_2_out);
  or or_3 (out_7, and_5_out, and_6_out);
endmodule

module AddMachine (
  output [7:0] out_1,
  output [7:0] out_2
);

  wire clock_1_out;

  Register register_1 (.D(out_1), .clk(clock_1_out), .Q(out_2));  // open: en, clr
  Clock clock_1 (.out(clock_1_out));
  Adder adder_1 (.a(out_2), .b(8'h1), .out(out_1));  // open: cin, cout
endmodule
