// Logisim project Part2.circ as structural Verilog: 7 circuits, main circuit main
module main (
  input  [15:0] in_1,
  input  [3:0] in_2,
  output [15:0] out_3
);

  Rotr rotr_1 (.A(in_1), .B(in_2), .rotrOutput(out_3));  // open: Output1, Output2, Output4
endmodule

module Ex4 (
  input  [7:0] In1,
  output Out1,
  output [7:0] Out2
);

  not not_1 (Out2[7], In1[7]);
  and and_1 (Out1, In1[0], In1[7]);

  assign Out2[6:0] = In1[6:0];

  // Other names for the same wires on the sheet: bit7 = In1[7]; bit0 = In1[0]; middle[5:0] = In1[6:1]
endmodule

module Rotr (
  input  [15:0] A,
  input  [3:0] B,
  output [15:0] Output1,
  output [15:0] Output2,
  output [15:0] Output4,
  output [15:0] rotrOutput
);

  rotr1 rotr1_1 (.Main(A), .Sbit(B[0]), .out_3(Output1));
  rotr2 rotr2_1 (.Main(Output1), .SBit(B[1]), .out_3(Output2));
  rotr4 rotr4_1 (.Main(Output2), .Sbit(B[2]), .out_3(Output4));
  rotr8 rotr8_1 (.Main(Output4), .Sbit(B[3]), .out_3(rotrOutput));

  // Other names for the same wires on the sheet: rotate1 = B[0]; rotate2 = B[1]; rotate3 = B[2]; rotate4 = B[3]
endmodule

module rotr1 (
  input  [15:0] Main,
  input  Sbit,
  output [15:0] out_3
);

  Multiplexer #(.width(16), .enable("false")) multiplexer_1 (
    .in0(Main), .in1({Main[0], Main[15:1]}), .out(out_3), .sel(Sbit));
endmodule

module rotr2 (
  input  [15:0] Main,
  input  SBit,
  output [15:0] out_3
);

  Multiplexer #(.width(16), .enable("false")) multiplexer_1 (
    .in0(Main), .in1({Main[1:0], Main[15:2]}), .out(out_3), .sel(SBit));
endmodule

module rotr4 (
  input  [15:0] Main,
  input  Sbit,
  output [15:0] out_3
);

  Multiplexer #(.width(16), .enable("false")) multiplexer_1 (
    .in0(Main), .in1({Main[3:0], Main[15:4]}), .out(out_3), .sel(Sbit));
endmodule

module rotr8 (
  input  [15:0] Main,
  input  Sbit,
  output [15:0] out_3
);

  Multiplexer #(.width(16), .enable("false")) multiplexer_1 (
    .in0(Main), .in1({Main[7:0], Main[15:8]}), .out(out_3), .sel(Sbit));
endmodule
