// Logisim project checkof.circ as structural Verilog: 7 circuits, main circuit main
module main (
  input  in_1,
  input  in_2,
  input  in_3,
  input  in_4,
  input  in_5,
  input  in_6,
  input  in_7,
  input  in_8,
  input  in_9,
  input  in_10,
  input  in_11,
  input  in_12,
  input  in_13,
  input  in_14,
  input  in_15,
  output [7:0] out_16,
  output [7:0] out_17,
  output out_18,
  output out_19,
  output out_20,
  output out_21,
  output out_22
);

  NAND1 nand1_1 (.in_1(in_1), .YO(in_2), .out_3(out_18));
  NOR1 nor1_1 (.in_1(in_3), .in_2(in_5), .out_3(out_19));
  XOR1 xor1_1 (.a(in_9), .b(in_11), .out_3(out_21));
  TWO2ONE two2one_1 (.in_1(in_13), .in_2(in_14), .in_3(in_15), .out_4(out_22));
  AddMachine addmachine_1 (.out_1(out_16), .out_2(out_17));
  FOUR2ONE four2one_1 (.A(in_4), .B(in_4), .C(in_7), .D(in_8), .S1(in_10), .S2(in_12), .out_7(out_20));

  assign in_6 = in_4;
endmodule

module NAND1 (
  input  in_1,
  input  YO,
  output out_3
);

  wire AND1_out;

  and AND1 (AND1_out, in_1, YO);
  not not_1 (out_3, AND1_out);
endmodule

module NOR1 (
  input  in_1,
  input  in_2,
  output out_3
);

  wire or_1_out;

  or or_1 (or_1_out, in_1, in_2);
  not not_1 (out_3, or_1_out);
endmodule

module XOR1 (
  input  a,
  input  b,
  output out_3
);

  wire and_1_out, and_2_out, not_1_out, not_2_out;

  not not_1 (not_1_out, a);
  not not_2 (not_2_out, b);
  and and_1 (and_1_out, a, not_2_out);
  and and_2 (and_2_out, not_1_out, b);
  or or_1 (out_3, and_1_out, and_2_out);
endmodule

module TWO2ONE (
  input  in_1,
  input  in_2,
  input  in_3,
  output out_4
);

  wire and_1_out, and_2_out, not_1_out;

  not not_1 (not_1_out, in_2);
  and and_1 (and_1_out, in_1, not_1_out);
  and and_2 (and_2_out, in_2, in_3);
  or or_1 (out_4, and_1_out, and_2_out);
endmodule

module FOUR2ONE (
  input  A,
  input  B,
  input  C,
  input  D,
  input  S1,
  input  S2,
  output out_7
);

  wire and_1_out, and_2_out, and_3_out, and_4_out, not_1_out, not_2_out;

  not not_1 (not_1_out, S1);
  not not_2 (not_2_out, S2);
  and and_1 (and_1_out, A, not_1_out, not_2_out);
  and and_2 (and_2_out, B, S2, not_1_out);
  and and_3 (and_3_out, not_2_out, C, S1);
  and and_4 (and_4_out, S2, D, S1);
  and and_5 (and_4_out, S2, D, S1);
  or or_1 (out_7, and_1_out, and_2_out, and_3_out, and_4_out);
endmodule

module AddMachine (
  output [7:0] out_1,
  output [7:0] out_2
);

  wire clock1_out;

  Adder adder_1 (.a(8'h1), .b(out_2), .out(out_1));  // open: cin, cout
  Clock clock1 (.out(clock1_out));
  Register register1 (.D(out_1), .clk(clock1_out), .Q(out_2));  // open: en, clr
endmodule
